# Fritzing sketch schema (saved by Fritzing 0.9.10b)

parts:
  Part1 = Arduino Nano (Rev3.0) (ICSP)
  Part3 = NRF24L01+ Breakout Board
  C1 = Electrolytic Capacitor [capacitance=100μF voltage=35V package="0807 [SMD, electrolytic]"]  # not connected
  Mod1 = Amica NodeMCU DEVKIT 1.0
  Part5 = NRF24L01+ Breakout Board
  C2 = Electrolytic Capacitor [capacitance=100μF voltage=35V package="0807 [SMD, electrolytic]"]  # not connected
  Part6 = Arduino Nano (Rev3.0) (ICSP)
  Part7 = NRF24L01+ Breakout Board
  C3 = Electrolytic Capacitor [capacitance=100μF voltage=35V package="0807 [SMD, electrolytic]"]  # not connected
  RHT1 = Humidity and Temperature Sensor RHT03
  Part8 = Breakout Board for Electret Microphone

nets:
  GND: Part1.GND, Part3.GND, RHT1.GND_2
  N1: Part1.D2, RHT1.Data-signal
  N2: Part1.D8, Part3.CS
  N3: Part1.D9, Part3.CE
  N4: Part1.D11/MOSI, Part3.MOSI
  N5: Part1.D12/MISO, Part3.MISO
  VIN: Part1.VIN, RHT1.Vcc
  3V3: Part1.3V3, Part3.VCC
  N6: Part1.D13/SCK, Part3.SCK
  N7: Mod1.pin6, Part5.MOSI
  N8: Mod1.pin7, Part5.MISO
  N9: Mod1.pin8, Part5.SCK
  N10: Mod1.pin_9, Mod1.pin_29, Part5.GND
  N11: Mod1.pin_10, Mod1.pin_26, Part5.VCC
  N12: Mod1.pin_11, Part5.CE
  N13: Mod1.pin_13, Part5.CS
  GND_2: Part6.GND, Part7.GND, Part8.GND
  N14: Part6.D8, Part7.CS
  N15: Part6.D9, Part7.CE
  N16: Part6.D11/MOSI, Part7.MOSI
  N17: Part6.D12/MISO, Part7.MISO
  VIN_2: Part6.VIN, Part8.VCC
  N18: Part6.A0, Part8.AUD
  3V3_2: Part6.3V3, Part7.VCC
  N19: Part6.D13/SCK, Part7.SCK
